// Logisim project ALU.circ as structural Verilog: 8 circuits, main circuit main
module main (
  input  [31:0] a,
  input  [31:0] b,
  input  [3:0] aluop,
  input  output_inverted,
  input  output_inc,
  input  clk,
  input  rst,
  output [31:0] res_low,
  output [31:0] res_high,
  output done
);

  wire [4:0] bit_extender_3_out;
  wire [31:0] divisor_1_quotient, divisor_1_remainder;
  wire [63:0] adder_1_out, and_1_out, bit_extender_1_out, bit_extender_2_out, multiplexer_1_out,
       multiplexer_2_out, not_1_out, or_1_out, rotr_1_out_3, s_l_l_1_out_3, s_r_a_1_out_3, s_r_l_1_out_3,
       subtractor_1_out, xor_1_out;

  assign bit_extender_1_out = {{32{1'b0}}, a};  // Bit_Extender bit_extender_1
  assign bit_extender_2_out = {{32{1'b0}}, b};  // Bit_Extender bit_extender_2
  Bit_Extender #(.in_width(32), .out_width(5), .\type ("zero")) bit_extender_3 (.in(b), .out(bit_extender_3_out));
  Adder #(.width(64)) adder_1 (.a(bit_extender_1_out), .b(bit_extender_2_out), .out(adder_1_out));  // open: cin, cout
  Subtractor #(.width(64)) subtractor_1 (
    .a(bit_extender_1_out), .b(bit_extender_2_out), .out(subtractor_1_out));  // open: bin, bout
  assign and_1_out = bit_extender_1_out & bit_extender_2_out;  // AND_Gate and_1, 64 bits wide
  assign or_1_out = bit_extender_1_out | bit_extender_2_out;  // OR_Gate or_1, 64 bits wide
  assign xor_1_out = bit_extender_1_out ^ bit_extender_2_out;  // XOR_Gate xor_1, 64 bits wide
  divisor divisor_1 (
    .divisor(a), .dividend(b), .start(rst), .clk(clk), .quotient(divisor_1_quotient),
    .remainder(divisor_1_remainder));  // open: done
  CLO clo_1 (.in1(a), .S(rst), .clk(clk));  // open: En, cnt, D
  CLZ clz_1 ();  // open: in1, S, clk, En, cnt, D
  s_l_l s_l_l_1 (.A(a), .shamt(bit_extender_3_out), .out_3(s_l_l_1_out_3));
  s_r_l s_r_l_1 (.A(a), .shamt(bit_extender_3_out), .out_3(s_r_l_1_out_3));
  s_r_a s_r_a_1 (.A(a), .shamt(bit_extender_3_out), .out_3(s_r_a_1_out_3));
  rotr rotr_1 (.A(a), .shamt(bit_extender_3_out), .out_3(rotr_1_out_3));
  Multiplexer #(.select(4), .width(64)) multiplexer_1 (
    .in0(adder_1_out), .in1(subtractor_1_out), .in3({divisor_1_remainder, divisor_1_quotient}),
    .in4(and_1_out), .in5(or_1_out), .in6(xor_1_out), .in7(xor_1_out), .in9(s_l_l_1_out_3),
    .in10(s_r_l_1_out_3), .in11(s_r_a_1_out_3), .in12(rotr_1_out_3), .out(multiplexer_1_out), .sel(aluop));  // open: in2, in8, in13, in14, in15
  assign not_1_out = ~multiplexer_1_out;  // NOT_Gate not_1, 64 bits wide
  Multiplexer #(.width(64)) multiplexer_2 (
    .in0(multiplexer_1_out), .in1(not_1_out), .out(multiplexer_2_out), .sel(output_inverted));
  Adder #(.width(64)) adder_2 (
    .a(multiplexer_2_out), .b({64{1'b0}}), .out({res_high, res_low}), .cin(output_inc));  // open: cout

  // Notes on the sheet:
  //   a: initial=0xb84d4170
endmodule

module divisor (
  input  [31:0] divisor,
  input  [31:0] dividend,
  input  start,
  input  clk,
  output [31:0] quotient,
  output [31:0] remainder,
  output done
);

  wire and_1_out, bitselector_1_out, comparator_1_eq, comparator_2_lt, not_1_out, not_2_out;
  wire [6:0] counter_q, multiplexer_4_out, multiplexer_8_out, subtractor_1_out;
  wire [31:0] A_q, adder_1_out, B_q, bit_extender_1_out, multiplexer_1_out, multiplexer_2_out,
       multiplexer_3_out, multiplexer_5_out, multiplexer_6_out, multiplexer_7_out, multiplexer_9_out,
       multiplexer_10_out, or_1_out, Q_q, shifter_1_out, shifter_2_out, subtractor_2_out;

  Multiplexer #(.width(32)) multiplexer_1 (
    .in0(multiplexer_9_out), .in1({32{1'b0}}), .out(multiplexer_1_out), .sel(start));
  Multiplexer #(.width(32)) multiplexer_2 (.in0(B_q), .in1(divisor), .out(multiplexer_2_out), .sel(start));
  Multiplexer #(.width(32)) multiplexer_3 (
    .in0(multiplexer_10_out), .in1(dividend), .out(multiplexer_3_out), .sel(start));
  Multiplexer #(.width(7)) multiplexer_4 (
    .in0(multiplexer_8_out), .in1(7'b0100000), .out(multiplexer_4_out), .sel(start));
  Subtractor #(.width(7)) subtractor_1 (.a(counter_q), .b(7'b0000001), .out(subtractor_1_out));  // open: bin, bout
  Multiplexer #(.width(32)) multiplexer_5 (.in0(multiplexer_1_out), .in1(A_q), .out(multiplexer_5_out), .sel(done));
  Multiplexer #(.width(32)) multiplexer_6 (.in0(multiplexer_2_out), .in1(B_q), .out(multiplexer_6_out), .sel(done));
  Multiplexer #(.width(32)) multiplexer_7 (.in0(multiplexer_3_out), .in1(Q_q), .out(multiplexer_7_out), .sel(done));
  Register #(.width(32)) A (.D(multiplexer_5_out), .en(1'b1), .clk(clk), .Q(A_q));  // open: clr
  Register #(.width(32)) B (.D(multiplexer_6_out), .en(1'b1), .clk(clk), .Q(B_q));  // open: clr
  Register #(.width(32)) Q (.D(multiplexer_7_out), .en(1'b1), .clk(clk), .Q(Q_q));  // open: clr
  Register #(.width(7)) counter (.D(multiplexer_4_out), .en(1'b1), .clk(clk), .Q(counter_q));  // open: clr
  Shifter #(.width(32)) shifter_1 (.in(A_q), .\dist (5'b00001), .out(shifter_1_out));
  BitSelector #(.width(32)) bitselector_1 (.in(Q_q), .out(bitselector_1_out), .sel({5{1'b1}}));
  Comparator #(.width(7)) comparator_1 (.a(counter_q), .b({7{1'b0}}), .eq(comparator_1_eq));  // open: gt, lt
  assign bit_extender_1_out = {{31{1'b0}}, bitselector_1_out};  // Bit_Extender bit_extender_1
  Adder #(.width(32)) adder_1 (.a(shifter_1_out), .b(bit_extender_1_out), .out(adder_1_out));  // open: cin, cout
  Shifter #(.width(32)) shifter_2 (.in(Q_q), .\dist (5'b00001), .out(shifter_2_out));
  Multiplexer #(.width(7)) multiplexer_8 (
    .in0(subtractor_1_out), .in1(counter_q), .out(multiplexer_8_out), .sel(comparator_1_eq));
  Subtractor #(.width(32)) subtractor_2 (.a(adder_1_out), .b(B_q), .out(subtractor_2_out));  // open: bin, bout
  Comparator #(.width(32)) comparator_2 (.a(adder_1_out), .b(B_q), .lt(comparator_2_lt));  // open: gt, eq
  not not_1 (not_1_out, comparator_2_lt);
  assign or_1_out = shifter_2_out | 32'h1;  // OR_Gate or_1, 32 bits wide
  and and_1 (and_1_out, comparator_1_eq, not_2_out);
  not not_2 (not_2_out, start);
  Multiplexer #(.width(32)) multiplexer_9 (
    .in0(adder_1_out), .in1(subtractor_2_out), .out(multiplexer_9_out), .sel(not_1_out));
  Multiplexer #(.width(32)) multiplexer_10 (
    .in0(shifter_2_out), .in1(or_1_out), .out(multiplexer_10_out), .sel(not_1_out));
  Multiplexer #(.width(32)) multiplexer_11 (.in1(Q_q), .out(quotient), .sel(and_1_out));  // open: in0
  Multiplexer #(.width(32)) multiplexer_12 (.in1(A_q), .out(remainder), .sel(and_1_out));  // open: in0
  Multiplexer multiplexer_13 (.in0(1'b0), .in1(1'b1), .out(done), .sel(and_1_out));

  // Notes on the sheet:
  //   divisor: initial=0x92153524
  //   clk: initial=0x1
endmodule

module rotr (
  input  [31:0] A,
  input  [4:0] shamt,
  output [63:0] out_3
);

  wire [1:0] lsb2;
  wire [3:0] lsb4;
  wire [7:0] lsb8;
  wire [15:0] lsb16;
  wire [47:0] shift_16;
  wire [55:0] shift_8;
  wire [59:0] shift_4;
  wire [61:0] shift_2;
  wire [63:0] extended_64;

  assign extended_64 = {{32{1'b0}}, A};  // Bit_Extender bit_extender_1
  Multiplexer #(.width(64)) multiplexer_1 (
    .in0({shift_16, lsb16}), .in1({lsb16, shift_16}), .out(out_3), .sel(shamt[4]));
  Multiplexer #(.width(64)) multiplexer_2 (
    .in0(extended_64), .in1({extended_64[0], extended_64[63:1]}), .out({shift_2, lsb2}), .sel(shamt[0]));
  Multiplexer #(.width(64)) multiplexer_3 (
    .in0({shift_2, lsb2}), .in1({lsb2, shift_2}), .out({shift_4, lsb4}), .sel(shamt[1]));
  Multiplexer #(.width(64)) multiplexer_4 (
    .in0({shift_4, lsb4}), .in1({lsb4, shift_4}), .out({shift_8, lsb8}), .sel(shamt[2]));
  Multiplexer #(.width(64)) multiplexer_5 (
    .in0({shift_8, lsb8}), .in1({lsb8, shift_8}), .out({shift_16, lsb16}), .sel(shamt[3]));

  // Other names for the same wires on the sheet: b0 = shamt[0]; b1 = shamt[1]; b2 = shamt[2]; b3 = shamt[3];
  //   b4 = shamt[4]; shift_1[63:0] = {extended_64[0], extended_64[63:1]}; lsb1 = extended_64[0];
  //   stage_1[63:0] = {shift_2, lsb2}; stage_2[63:0] = {shift_4, lsb4}; shift_4[63:60] = lsb4;
  //   stage_4[63:0] = {shift_8, lsb8}; shift_8[63:56] = lsb8; stage_8[63:0] = {shift_16, lsb16};
  //   shift_2[63:62] = lsb2; shift_16[63:48] = lsb16; stage_16[63:0] = out_3
endmodule

module s_r_a (
  input  [31:0] A,
  input  [4:0] shamt,
  output [63:0] out_3
);

  wire [1:0] stage_1;
  wire [3:0] stage_2;
  wire [7:0] stage_4;
  wire [15:0] stage_8;
  wire [63:0] extended_64, shift_2, shift_4, shift_8, shift_16;

  assign extended_64 = {{32{A[31]}}, A};  // Bit_Extender bit_extender_1
  Multiplexer #(.width(64)) multiplexer_1 (
    .in0({shift_16[63], shift_16[46:0], stage_8}), .in1({{17{shift_16[63]}}, shift_16[46:0]}), .out(out_3),
    .sel(shamt[4]));
  Multiplexer #(.width(64)) multiplexer_2 (
    .in0(extended_64), .in1({{2{extended_64[63]}}, extended_64[62:1]}),
    .out({shift_2[63], shift_2[60:0], stage_1}), .sel(shamt[0]));
  Multiplexer #(.width(64)) multiplexer_3 (
    .in0({shift_2[63], shift_2[60:0], stage_1}), .in1({{3{shift_2[63]}}, shift_2[60:0]}),
    .out({shift_4[63], shift_4[58:0], stage_2}), .sel(shamt[1]));
  Multiplexer #(.width(64)) multiplexer_4 (
    .in0({shift_4[63], shift_4[58:0], stage_2}), .in1({{5{shift_4[63]}}, shift_4[58:0]}),
    .out({shift_8[63], shift_8[54:0], stage_4}), .sel(shamt[2]));
  Multiplexer #(.width(64)) multiplexer_5 (
    .in0({shift_8[63], shift_8[54:0], stage_4}), .in1({{9{shift_8[63]}}, shift_8[54:0]}),
    .out({shift_16[63], shift_16[46:0], stage_8}), .sel(shamt[3]));

  // Other names for the same wires on the sheet: b0 = shamt[0]; b1 = shamt[1]; b2 = shamt[2]; b3 = shamt[3];
  //   b4 = shamt[4]; shift_1[63:0] = {{2{extended_64[63]}}, extended_64[62:1]};
  //   stage_1[63:2] = {shift_2[63], shift_2[60:0]}; shift_2[62:61] = {2{shift_2[63]}};
  //   stage_2[63:4] = {shift_4[63], shift_4[58:0]}; shift_4[62:59] = {4{shift_4[63]}};
  //   stage_4[63:8] = {shift_8[63], shift_8[54:0]}; shift_8[62:55] = {8{shift_8[63]}};
  //   stage_8[63:16] = {shift_16[63], shift_16[46:0]}; shift_16[62:47] = {16{shift_16[63]}}; stage_16[63:0] = out_3
endmodule

module CLZ (
  input  [31:0] in1,
  input  S,
  input  clk,
  input  En,
  output [4:0] cnt,
  output D
);

  wire CBZ, INIT, not_1_out, not_2_out, not_3_out, not_4_out, not_5_out, not_6_out, or_1_out, or_2_out,
       or_3_out, or_4_out, or_5_out, R0_bit0, RN_eq_0, SHIFT, T0, T1, T2, T3, T4, T5;
  wire [4:0] adder_1_out, controlled_buffer_1_out, R1_q, RN_dec, RN_q;
  wire [31:0] controlled_buffer_3_out, R0_q, shifter_1_out;

  or or_1 (or_1_out, T4, T1);
  or or_2 (or_2_out, T0, SHIFT);
  D_Flip_Flop u_INIT (.D(or_1_out), .clk(clk), .Q(INIT));  // open: Qn, preset, reset
  D_Flip_Flop CBO (.D(or_2_out), .clk(clk), .Q(CBZ));  // open: Qn, preset, reset
  D_Flip_Flop u_SHIFT (.D(T5), .clk(clk), .Q(SHIFT));  // open: Qn, preset, reset
  not not_1 (not_1_out, RN_eq_0);
  not not_2 (not_2_out, RN_eq_0);
  not not_3 (not_3_out, R0_bit0);
  not not_4 (not_4_out, S);
  not not_5 (not_5_out, RN_eq_0);
  and and_1 (T0, INIT, S);
  and and_2 (T1, CBZ, En, RN_eq_0);
  and and_3 (T2, CBZ, not_1_out, R0_bit0);
  and and_4 (T3, CBZ, not_2_out, not_3_out);
  and and_5 (T4, INIT, not_4_out);
  and and_6 (T5, CBZ, not_5_out);
  assign controlled_buffer_1_out = T0 ? {5{1'b1}} : 5'bz;  // Controlled_Buffer controlled_buffer_1
  assign controlled_buffer_1_out = SHIFT ? RN_dec : 5'bz;  // Controlled_Buffer controlled_buffer_2
  or or_3 (or_3_out, T0, SHIFT);
  Register #(.width(5)) RN (.D(controlled_buffer_1_out), .en(or_3_out), .clk(clk), .Q(RN_q));  // open: clr
  or or_4 (or_4_out, T0, SHIFT);
  assign controlled_buffer_3_out = T0 ? in1 : 32'bz;  // Controlled_Buffer controlled_buffer_3
  assign controlled_buffer_3_out = SHIFT ? shifter_1_out : 32'bz;  // Controlled_Buffer controlled_buffer_4
  Subtractor #(.width(5)) subtractor_1 (.a(RN_q), .b(5'b00001), .out(RN_dec));  // open: bin, bout
  Comparator #(.width(5)) comparator_1 (.a(RN_q), .b({5{1'b0}}), .eq(RN_eq_0));  // open: gt, lt
  Register #(.width(32)) R0 (.D(controlled_buffer_3_out), .en(or_4_out), .clk(clk), .Q(R0_q));  // open: clr
  or or_5 (or_5_out, T3, T0);
  not not_6 (not_6_out, R0_q[0]);
  Register #(.width(5)) R1 (.D(adder_1_out), .en(T2), .clk(clk), .Q(R1_q), .clr(or_5_out));
  Register #(.width(5)) R2 (.D(R1_q), .en(T1), .clk(clk), .Q(cnt));  // open: clr
  and and_7 (R0_bit0, 1'b1, not_6_out);
  Shifter #(.shift("lr"), .width(32)) shifter_1 (.in(R0_q), .\dist (5'b00001), .out(shifter_1_out));
  Register #(.width(1)) RD (.D(1'b1), .en(T1), .clk(clk), .Q(D), .clr(T0));
  Adder #(.width(5)) adder_1 (.a(R1_q), .b(5'b00001), .out(adder_1_out));  // open: cin, cout
endmodule

module s_r_l (
  input  [31:0] A,
  input  [4:0] shamt,
  output [63:0] out_3
);

  wire [1:0] stage_1;
  wire [3:0] stage_2;
  wire [7:0] stage_4;
  wire [15:0] stage_8;
  wire [47:0] shift_16;
  wire [55:0] shift_8;
  wire [59:0] shift_4;
  wire [61:0] shift_2;
  wire [63:0] extended_64;

  assign extended_64 = {{32{1'b0}}, A};  // Bit_Extender bit_extender_1
  Multiplexer #(.width(64)) multiplexer_1 (
    .in0({shift_16, stage_8}), .in1({{16{1'b0}}, shift_16}), .out(out_3), .sel(shamt[4]));
  Multiplexer #(.width(64)) multiplexer_2 (
    .in0(extended_64), .in1({1'b0, extended_64[63:1]}), .out({shift_2, stage_1}), .sel(shamt[0]));
  Multiplexer #(.width(64)) multiplexer_3 (
    .in0({shift_2, stage_1}), .in1({2'b00, shift_2}), .out({shift_4, stage_2}), .sel(shamt[1]));
  Multiplexer #(.width(64)) multiplexer_4 (
    .in0({shift_4, stage_2}), .in1({4'b0000, shift_4}), .out({shift_8, stage_4}), .sel(shamt[2]));
  Multiplexer #(.width(64)) multiplexer_5 (
    .in0({shift_8, stage_4}), .in1({{8{1'b0}}, shift_8}), .out({shift_16, stage_8}), .sel(shamt[3]));

  // Other names for the same wires on the sheet: b0 = shamt[0]; b1 = shamt[1]; b2 = shamt[2]; b3 = shamt[3];
  //   b4 = shamt[4]; shift_1[62:0] = extended_64[63:1]; stage_1[63:2] = shift_2; stage_2[63:4] = shift_4;
  //   stage_4[63:8] = shift_8; stage_8[63:16] = shift_16; stage_16[63:0] = out_3
endmodule

module CLO (
  input  [31:0] in1,
  input  S,
  input  clk,
  input  En,
  output [4:0] cnt,
  output D
);

  wire CBO, INIT, not_1_out, not_2_out, not_3_out, not_4_out, not_5_out, or_1_out, or_2_out, or_3_out,
       or_4_out, or_5_out, R0_bit0, RN_eq_0, SHIFT, T0, T1, T2, T3, T4, T5;
  wire [4:0] adder_1_out, controlled_buffer_1_out, R1_q, RN_dec, RN_q;
  wire [31:0] controlled_buffer_3_out, R0_q, shifter_1_out;

  or or_1 (or_1_out, T4, T1);
  or or_2 (or_2_out, T0, SHIFT);
  D_Flip_Flop u_INIT (.D(or_1_out), .clk(clk), .Q(INIT));  // open: Qn, preset, reset
  D_Flip_Flop u_CBO (.D(or_2_out), .clk(clk), .Q(CBO));  // open: Qn, preset, reset
  D_Flip_Flop u_SHIFT (.D(T5), .clk(clk), .Q(SHIFT));  // open: Qn, preset, reset
  not not_1 (not_1_out, RN_eq_0);
  not not_2 (not_2_out, RN_eq_0);
  not not_3 (not_3_out, R0_bit0);
  not not_4 (not_4_out, S);
  not not_5 (not_5_out, RN_eq_0);
  and and_1 (T0, INIT, S);
  and and_2 (T1, CBO, En, RN_eq_0);
  and and_3 (T2, CBO, not_1_out, R0_bit0);
  and and_4 (T3, CBO, not_2_out, not_3_out);
  and and_5 (T4, INIT, not_4_out);
  and and_6 (T5, CBO, not_5_out);
  assign controlled_buffer_1_out = T0 ? {5{1'b1}} : 5'bz;  // Controlled_Buffer controlled_buffer_1
  assign controlled_buffer_1_out = SHIFT ? RN_dec : 5'bz;  // Controlled_Buffer controlled_buffer_2
  or or_3 (or_3_out, T0, SHIFT);
  Register #(.width(5)) RN (.D(controlled_buffer_1_out), .en(or_3_out), .clk(clk), .Q(RN_q));  // open: clr
  or or_4 (or_4_out, T0, SHIFT);
  assign controlled_buffer_3_out = T0 ? in1 : 32'bz;  // Controlled_Buffer controlled_buffer_3
  assign controlled_buffer_3_out = SHIFT ? shifter_1_out : 32'bz;  // Controlled_Buffer controlled_buffer_4
  Subtractor #(.width(5)) subtractor_1 (.a(RN_q), .b(5'b00001), .out(RN_dec));  // open: bin, bout
  Comparator #(.width(5)) comparator_1 (.a(RN_q), .b({5{1'b0}}), .eq(RN_eq_0));  // open: gt, lt
  Register #(.width(32)) R0 (.D(controlled_buffer_3_out), .en(or_4_out), .clk(clk), .Q(R0_q));  // open: clr
  or or_5 (or_5_out, T3, T0);
  and and_7 (R0_bit0, 1'b1, R0_q[0]);
  Register #(.width(5)) R1 (.D(adder_1_out), .en(T2), .clk(clk), .Q(R1_q), .clr(or_5_out));
  Register #(.width(5)) R2 (.D(R1_q), .en(T1), .clk(clk), .Q(cnt));  // open: clr
  Shifter #(.shift("lr"), .width(32)) shifter_1 (.in(R0_q), .\dist (5'b00001), .out(shifter_1_out));
  Register #(.width(1)) RD (.D(1'b1), .en(T1), .clk(clk), .Q(D), .clr(T0));
  Adder #(.width(5)) adder_1 (.a(R1_q), .b(5'b00001), .out(adder_1_out));  // open: cin, cout
endmodule

module s_l_l (
  input  [31:0] A,
  input  [4:0] shamt,
  output [63:0] out_3
);

  wire [63:0] extended_64;
  wire [63:2] shift_2;
  wire [63:4] shift_4;
  wire [63:7] shift_8;
  wire [63:16] shift_16;
  wire [63:48] stage_8;
  wire [63:57] stage_4;
  wire [63:60] stage_2;
  wire [63:62] stage_1;

  assign extended_64 = {{32{1'b0}}, A};  // Bit_Extender bit_extender_1
  Multiplexer #(.width(64)) multiplexer_1 (
    .in0({stage_8, shift_16}), .in1({shift_16, {16{1'b0}}}), .out(out_3), .sel(shamt[4]));
  Multiplexer #(.width(64)) multiplexer_2 (
    .in0(extended_64), .in1({extended_64[62:0], 1'b0}), .out({stage_1, shift_2}), .sel(shamt[0]));
  Multiplexer #(.width(64)) multiplexer_3 (
    .in0({stage_1, shift_2}), .in1({shift_2, 2'b00}), .out({stage_2, shift_4}), .sel(shamt[1]));
  Multiplexer #(.width(64)) multiplexer_4 (
    .in0({stage_2, shift_4}), .in1({shift_4, 4'b0000}), .out({stage_4, shift_8}), .sel(shamt[2]));
  Multiplexer #(.width(64)) multiplexer_5 (
    .in0({stage_4, shift_8}), .in1({shift_8, {7{1'b0}}}), .out({stage_8, shift_16}), .sel(shamt[3]));

  // Other names for the same wires on the sheet: b0 = shamt[0]; b1 = shamt[1]; b2 = shamt[2]; b3 = shamt[3];
  //   b4 = shamt[4]; shift_1[63:1] = extended_64[62:0]; stage_2[59:0] = shift_4; stage_4[56:0] = shift_8;
  //   stage_8[47:0] = shift_16; stage_1[61:0] = shift_2; stage_16[63:0] = out_3
endmodule
